# Fritzing sketch MiniAtlas (saved by Fritzing 0.9.10b)

parts:
  M1 = gear-motor
  M2 = gear-motor
  U2 = L9110 H-bridge module [part_number="L9110 H-bridge"]
  J10 = Wago 221-415
  J11 = Wago 221-415
  Composant5 = Arduino Mega 2560 (Rev3)
  S1 = Pololu QTR-8 Reflectabce Sensor array [package=THT]
  J15 = Basic Servo
  J16 = Basic Servo
  HC-1 = HC-12 Module
  Antenna1 = HC-12 Antenna  # not connected
  BAT1 = 18650 battery holder [package=battery-18650-kit]
  BAT2 = 18650 battery holder [package=battery-18650-kit]

nets:
  N1: M1.pin_1, U2.MOTOR_A-B
  N2: M1.pin_2, U2.MOTOR_A-A
  N3: M2.pin_1, U2.MOTOR_B-B
  N4: M2.pin_2, U2.MOTOR_B-A
  N5: U2.B-IA, Composant5.D9_PWM
  N6: U2.B-IB, Composant5.D6_PWM
  GND: U2.GND, Composant5.GND, S1.pin15, S1.pin17, HC-1.GND
  VCC: U2.VCC, Composant5.5V, S1.pin2, S1.pin22, HC-1.VCC
  N7: U2.A-IA, Composant5.D5_PWM
  N8: U2.A-IB, Composant5.D3_PWM
  N9: J10.Pin_3, J10.Pin_4, J10.Pin_5, BAT1.+
  N10: J11.Pin_1, J11.Pin_2, J11.Pin_3, J11.Pin_5, BAT2.-
  N11: Composant5.D12_PWM, HC-1.TXD
  N12: Composant5.D11_PWM, HC-1.RXD
  N13: Composant5.D2_PWM, J15.pulse
  N14: Composant5.D4_PWM, J16.pulse
  N15: Composant5.D38, S1.pin5
  N16: Composant5.D40, S1.pin6
  N17: Composant5.D42, S1.pin7
  N18: Composant5.D44, S1.pin8
  N19: Composant5.D46, S1.pin9
  N20: Composant5.D48, S1.pin10
  N21: Composant5.D50, S1.pin11
  N22: Composant5.D52, S1.pin12

custom parts:
  Wago 221-415: Wago 221-415 5 position splicing connector 12AWG.
  HC-12 Module: HC-12 433Mhz Module
  HC-12 Antenna: Antenna for HC-12 433Mhz Module
  18650 battery holder: 18650 Battery Holder identical to the dual battery version.
