# Fritzing sketch MiniAtlas (saved by Fritzing 0.9.10b)
breadboards: 1

parts:
  M1 = gear-motor
  M2 = gear-motor
  VCC2 = Battery  # not connected
  U1 = SWITCH_SPDT [package=kps-1290]  # not connected
  R1 = Resistor [tolerance=±5% resistance=220 package="0603 [SMD]"]  # not connected
  U2 = L9110 H-bridge module [part_number="L9110 H-bridge"]
  M3 = fc-51 [package=THT]
  M8 = fc-51 [package=THT]
  M9 = fc-51 [package=THT]
  M10 = fc-51 [package=THT]
  M11 = fc-51 [package=THT]
  J10 = Wago 221-415
  J11 = Wago 221-415
  J13 = Basic Servo
  J14 = Basic Servo
  Composant4 = FC-03 [chip_label=FC-03]
  Composant5 = Arduino Mega 2560 (Rev3)
  Composant6 = FC-03 [chip_label=FC-03]

nets:
  N1: M1.pin_1, U2.MOTOR_A-B
  N2: M1.pin_2, U2.MOTOR_A-A
  N3: M2.pin_1, U2.MOTOR_B-B
  N4: M2.pin_2, U2.MOTOR_B-A
  N5: U2.B-IA, Composant5.D9_PWM
  N6: U2.B-IB, Composant5.D6_PWM
  GND: U2.GND, M3.pin2, M8.pin2, M9.pin2, M10.pin2, M11.pin2, Composant4.pin_2, Composant5.GND, Composant6.pin_2
  VCC: U2.VCC, M3.pin3, M8.pin3, M9.pin3, M10.pin3, M11.pin3, Composant4.pin_1, Composant5.5V, Composant6.pin_1
  N7: U2.A-IA, Composant5.D5_PWM
  N8: U2.A-IB, Composant5.D3_PWM
  N9: M3.pin1, Composant5.D11_PWM
  N10: M8.pin1, Composant5.D13_PWM
  N11: M9.pin1, Composant5.D8_PWM
  N12: M10.pin1, Composant5.D10_PWM
  N13: M11.pin1, Composant5.D12_PWM
  N14: J10.Pin_3, J10.Pin_4
  N15: J11.Pin_2, J11.Pin_3
  N16: J13.pulse, Composant5.D2_PWM
  N17: J14.pulse, Composant5.D4_PWM
  N18: Composant4.pin_3, Composant5.D14/TX3
  N19: Composant4.pin_4, Composant5.A4
  N20: Composant5.A5, Composant6.pin_4
  N21: Composant5.D15/RX3, Composant6.pin_3

custom parts:
  Wago 221-415: Wago 221-415 5 position splicing connector 12AWG.
  FC-03: FC-03, LM393 IR Speed Sensor Encoder
